// Digital circuit Lab_02.dig as structural Verilog
module Lab_02 (
  input  PE,
  input  Red,
  input  Bateria,
  input  Sol,
  output Desenergizador,
  output Conmutador
);

  wire and_1_out, and_2_out, not_1_out, or_1_out;

  not not_1 (not_1_out, Bateria);
  or or_1 (or_1_out, Red, Sol);
  and and_1 (and_1_out, Red, Sol);
  and and_2 (and_2_out, or_1_out, not_1_out);
  or or_2 (Conmutador, and_1_out, and_2_out);

  assign Desenergizador = PE;
endmodule
