// Digital circuit 10-2.dig as structural Verilog
module _10_2 (
  input  clk_FSM,
  output _10_2
);

  wire and_1_out, and_2_out, and_3_out, and_4_out, and_5_out, and_7_out, and_8_out, nor_1_out, nor_2_out,
       nor_3_out, nor_4_out, nor_5_out, nor_6_out, nor_7_out, S;
  wire [3:0] counter_1_out;

  Counter #(.Bits(4)) counter_1 (.en(1'b1), .C(clk_FSM), .clr(S), .out(counter_1_out));  // open: ovf
  // Probe on counter_1_out
  and and_1 (and_1_out, counter_1_out[0], 1'b1);
  and and_2 (and_2_out, counter_1_out[1], 1'b1);
  nor nor_1 (nor_1_out, counter_1_out[2], 1'b0);
  and and_3 (and_3_out, counter_1_out[3], 1'b1);
  nor nor_2 (nor_2_out, counter_1_out[0], 1'b0);
  nor nor_3 (nor_3_out, counter_1_out[1], 1'b0);
  nor nor_4 (nor_4_out, counter_1_out[2], 1'b0);
  nor nor_5 (nor_5_out, counter_1_out[3], 1'b0);
  nor nor_6 (nor_6_out, counter_1_out[0], 1'b0);
  and and_4 (and_4_out, counter_1_out[1], 1'b1);
  nor nor_7 (nor_7_out, counter_1_out[2], 1'b0);
  and and_5 (and_5_out, counter_1_out[3], 1'b1);
  and and_6 (S, and_1_out, and_2_out, nor_1_out, and_3_out);
  and and_7 (and_7_out, nor_2_out, nor_3_out, nor_4_out, nor_5_out);
  and and_8 (and_8_out, nor_6_out, and_4_out, nor_7_out, and_5_out);
  or or_1 (_10_2, and_7_out, and_8_out);
endmodule
