// Digital circuit Comparador.dig as structural Verilog
module Comparador (
  input  [5:0] NA,
  input  [5:0] NB,
  input  [5:0] NC,
  input  [5:0] ND,
  output TA,
  output TB,
  output TC,
  output TD
);

  wire and_1_out, and_2_out, comparator_1_lt, comparator_2_lt, comparator_3_eq, comparator_3_gt,
       comparator_3_lt, or_1_out;
  wire [5:0] multiplexer_1_out, multiplexer_2_out;

  Comparator #(.Bits(6)) comparator_1 (.a(NA), .b(NB), .lt(comparator_1_lt));  // open: gt, eq
  Comparator #(.Bits(6)) comparator_2 (.a(NC), .b(ND), .lt(comparator_2_lt));  // open: gt, eq
  Multiplexer #(.Bits(6)) multiplexer_1 (.sel(comparator_1_lt), .in_0(NA), .in_1(NB), .out(multiplexer_1_out));
  Multiplexer #(.Bits(6)) multiplexer_2 (.sel(comparator_2_lt), .in_0(NC), .in_1(ND), .out(multiplexer_2_out));
  Comparator #(.Bits(6)) comparator_3 (
    .a(multiplexer_1_out), .b(multiplexer_2_out), .gt(comparator_3_gt), .eq(comparator_3_eq),
    .lt(comparator_3_lt));
  or or_1 (or_1_out, comparator_3_gt, comparator_3_eq);
  and and_1 (and_1_out, comparator_3_lt, comparator_2_lt);
  and and_2 (and_2_out, comparator_1_lt, or_1_out);
  Demultiplexer demultiplexer_1 (.sel(and_1_out), .in(comparator_3_lt), .out_0(TC), .out_1(TD));
  Demultiplexer demultiplexer_2 (.sel(and_2_out), .in(or_1_out), .out_0(TA), .out_1(TB));
endmodule
