// Digital circuit Contador.dig as structural Verilog
module Contador (
  input  clk_count,
  input  plus__plus,
  input  plus,
  input  in_4,
  input  in_6,
  output [5:0] Num,
  output [13:0] NUM_7S
);

  wire and_1_out, and_2_out, and_3_out, and_4_out, and_5_out, and_6_out, and_7_out, and_8_out, and_9_out,
       div_1_a0, div_1_a1, div_1_b0, div_1_b1, div_1_c0, div_1_c1, div_1_d0, div_1_d1, L, M, or_1_out,
       or_2_out, or_3_out, or_4_out, or_5_out, or_6_out;
  wire [5:0] counter_1_out, counter_2_out, counter_3_out, counter_4_out, sub_1_s, sub_2_s;

  and and_1 (and_1_out, plus__plus, clk_count);
  and and_2 (and_2_out, in_6, clk_count);
  Counter #(.Bits(6)) counter_1 (.en(L), .C(and_1_out), .clr(1'b0), .out(counter_1_out));  // open: ovf
  Counter #(.Bits(6)) counter_2 (.en(M), .C(and_2_out), .clr(1'b0), .out(counter_2_out));  // open: ovf
  Counter #(.Bits(6)) counter_3 (.en(L), .C(plus), .clr(1'b0), .out(counter_3_out));  // open: ovf
  Counter #(.Bits(6)) counter_4 (.en(M), .C(in_4), .clr(1'b0), .out(counter_4_out));  // open: ovf
  // Probe on counter_4_out
  // Probe on counter_1_out
  Sub #(.Bits(6)) sub_1 (.a(counter_1_out), .b(counter_2_out), .c_i(1'b0), .s(sub_1_s));  // open: c_o
  // Probe on counter_2_out
  // Probe on counter_3_out
  Sub #(.Bits(6)) sub_2 (.a(counter_3_out), .b(counter_4_out), .c_i(1'b0), .s(sub_2_s));  // open: c_o
  Add #(.Bits(6)) add_1 (.a(sub_1_s), .b(sub_2_s), .c_i(1'b0), .s(Num));  // open: c_o
  and and_3 (and_3_out, Num[0], 1'b1);
  and and_4 (and_4_out, Num[1], 1'b1);
  and and_5 (and_5_out, Num[2], 1'b1);
  and and_6 (and_6_out, Num[3], 1'b1);
  and and_7 (and_7_out, Num[4], 1'b1);
  and and_8 (and_8_out, Num[5], 1'b1);
  or or_1 (or_1_out, Num[0], 1'b0);
  or or_2 (or_2_out, Num[1], 1'b0);
  or or_3 (or_3_out, Num[2], 1'b0);
  or or_4 (or_4_out, Num[3], 1'b0);
  or or_5 (or_5_out, Num[4], 1'b0);
  or or_6 (or_6_out, Num[5], 1'b0);
  and and_9 (and_9_out, and_3_out, and_4_out, and_5_out, and_6_out, and_7_out, and_8_out);
  or or_7 (M, or_1_out, or_2_out, or_3_out, or_4_out, or_5_out, or_6_out);
  not not_1 (L, and_9_out);
  div div_1 (
    .NUM(Num), .A0(div_1_a0), .B0(div_1_b0), .C0(div_1_c0), .D0(div_1_d0), .A1(div_1_a1), .B1(div_1_b1),
    .C1(div_1_c1), .D1(div_1_d1));
  bcd_7S bcd_7s_1 (.A(div_1_a0), .B(div_1_b0), .C(div_1_c0), .D(div_1_d0), ._7S(NUM_7S[6:0]));
  bcd_7S bcd_7s_2 (.A(div_1_a1), .B(div_1_b1), .C(div_1_c1), .D(div_1_d1), ._7S(NUM_7S[13:7]));
  // Probe on NUM_7S[6:0]
endmodule
