// Digital circuit FSM.dig as structural Verilog
module FSM (
  input  clk_FF,
  input  TA,
  input  TB,
  input  TC,
  input  TD,
  output Q0,
  output Q1,
  output Q2,
  output Q3,
  output NQ0,
  output NQ1,
  output NQ2,
  output NQ3
);

  wire and_1_out, and_2_out, and_3_out, and_4_out, and_5_out, and_6_out, and_7_out, and_8_out, and_9_out,
       and_10_out, and_11_out, and_12_out, and_13_out, and_14_out, and_15_out, and_16_out, and_17_out,
       and_18_out, and_19_out, and_20_out, and_21_out, and_22_out, and_23_out, and_24_out, and_25_out,
       and_26_out, or_1_out, or_2_out, or_3_out, or_4_out, or_5_out, or_6_out, or_7_out, or_8_out, or_9_out,
       or_10_out, or_11_out, or_12_out, or_13_out, or_14_out, or_15_out, or_16_out, or_17_out, or_18_out;

  and and_1 (and_1_out, NQ3, NQ2, Q1, NQ0);
  and and_2 (and_2_out, NQ3, Q2, Q1, NQ0);
  and and_3 (and_3_out, Q3, Q2, NQ1, NQ0);
  and and_4 (and_4_out, Q3, NQ2, NQ1, Q0);
  and and_5 (and_5_out, NQ3, Q2, NQ1, NQ0);
  and and_6 (and_6_out, NQ3, NQ2, NQ1, Q0);
  and and_7 (and_7_out, Q3, NQ2, Q1, NQ0);
  and and_8 (and_8_out, NQ3, NQ2, NQ1, Q0);
  and and_9 (and_9_out, NQ3, NQ2, Q1, NQ0);
  and and_10 (and_10_out, Q3, NQ2, NQ1, NQ0);
  or or_1 (or_1_out, TC, TD);
  or or_2 (or_2_out, and_1_out, and_2_out);
  or or_3 (or_3_out, and_3_out, and_4_out);
  or or_4 (or_4_out, and_5_out, and_6_out);
  or or_5 (or_5_out, TA, TB);
  or or_6 (or_6_out, and_7_out, and_8_out);
  or or_7 (or_7_out, and_9_out, and_10_out);
  or or_8 (or_8_out, TA, TC);
  or or_9 (or_9_out, TB, TC);
  or or_10 (or_10_out, TA, TC, TD);
  or or_11 (or_11_out, TB, TC);
  or or_12 (or_12_out, TA, TB, TD);
  and and_11 (and_11_out, NQ3, NQ2, Q1, NQ0, or_5_out);
  and and_12 (and_12_out, TA, NQ3, Q2, Q1, NQ0);
  and and_13 (and_13_out, NQ3, Q2, Q1, NQ0, or_8_out);
  and and_14 (and_14_out, TA, NQ3, Q2, NQ1, NQ0);
  and and_15 (and_15_out, or_1_out, NQ0, NQ1, NQ2, NQ3);
  and and_16 (and_16_out, TA, or_2_out);
  and and_17 (and_17_out, TC, or_3_out);
  and and_18 (and_18_out, TD, or_4_out);
  and and_19 (and_19_out, TB, Q3, Q2, Q1, NQ0);
  and and_20 (and_20_out, TD, or_6_out);
  and and_21 (and_21_out, TB, or_7_out);
  and and_22 (and_22_out, TC, Q3, Q2, NQ1, NQ0);
  and and_23 (and_23_out, or_9_out, NQ3, NQ2, NQ1, NQ0);
  and and_24 (and_24_out, or_10_out, NQ3, Q2, NQ1, NQ0);
  and and_25 (and_25_out, or_11_out, NQ3, Q2, Q1, NQ0);
  and and_26 (and_26_out, or_12_out, NQ3, NQ2, Q1, NQ0);
  or or_13 (or_13_out, and_15_out, and_16_out);
  or or_14 (or_14_out, and_17_out, and_18_out);
  or or_15 (or_15_out, and_11_out, and_12_out, and_19_out);
  or or_16 (or_16_out, and_20_out, and_21_out);
  or or_17 (or_17_out, and_13_out, and_14_out, and_22_out);
  or or_18 (or_18_out, and_23_out, and_24_out, and_25_out, and_26_out);
  D_FF d_ff_1 (.D(or_13_out), .C(clk_FF), .Q(Q0), .nQ(NQ0));
  JK_FF jk_ff_1 (.J(or_14_out), .C(clk_FF), .K(or_15_out), .Q(Q1), .nQ(NQ1));
  JK_FF jk_ff_2 (.J(or_16_out), .C(clk_FF), .K(or_17_out), .Q(Q2), .nQ(NQ2));
  D_FF d_ff_2 (.D(or_18_out), .C(clk_FF), .Q(Q3), .nQ(NQ3));

  // Other names for the same wires on the sheet: clk = clk_FF
endmodule
