// Digital circuit MUX.dig as structural Verilog
module MUX (
  input  clk_MUX,
  input  [13:0] _7SA,
  input  [13:0] _7SB,
  input  [13:0] _7SC,
  input  [13:0] _7SD,
  output a,
  output b,
  output c,
  output d,
  output e,
  output f,
  output g,
  output EA0,
  output EA1,
  output EB0,
  output EB1,
  output EC0,
  output EC1,
  output ED0,
  output ED1
);

  wire and_1_out, and_2_out, and_3_out, NX0, NX1, NX2, or_1_out, X0, X1, X2, xor_1_out;
  wire [6:0] multiplexer_1_out;

  and and_1 (and_1_out, X2, NX0);
  and and_2 (and_2_out, X0, NX2, X1);
  and and_3 (and_3_out, X2, NX1);
  xor xor_1 (xor_1_out, X1, X0);
  or or_1 (or_1_out, and_1_out, and_2_out, and_3_out);
  D_FF d_ff_1 (.D(NX0), .C(clk_MUX), .Q(X0), .nQ(NX0));
  D_FF d_ff_2 (.D(xor_1_out), .C(clk_MUX), .Q(X1), .nQ(NX1));
  D_FF d_ff_3 (.D(or_1_out), .C(clk_MUX), .Q(X2), .nQ(NX2));
  Multiplexer #(.Selector_Bits(3), .Bits(7)) multiplexer_1 (
    .sel({X2, X1, X0}), .in_0(_7SA[6:0]), .in_1(_7SA[13:7]), .in_2(_7SB[6:0]), .in_3(_7SB[13:7]),
    .in_4(_7SC[6:0]), .in_5(_7SC[13:7]), .in_6(_7SD[6:0]), .in_7(_7SD[13:7]), .out(multiplexer_1_out));
  nor nor_1 (EA1, X2, X1, NX0);
  nor nor_2 (EB1, X2, NX1, NX0);
  nor nor_3 (EC1, NX2, X1, NX0);
  nor nor_4 (ED1, NX2, NX1, NX0);
  not not_1 (a, multiplexer_1_out[0]);
  not not_2 (b, multiplexer_1_out[1]);
  not not_3 (c, multiplexer_1_out[2]);
  not not_4 (d, multiplexer_1_out[3]);
  not not_5 (e, multiplexer_1_out[4]);
  not not_6 (f, multiplexer_1_out[5]);
  not not_7 (g, multiplexer_1_out[6]);
  nor nor_5 (EA0, X2, X1, X0);
  nor nor_6 (EB0, X2, NX1, X0);
  nor nor_7 (EC0, NX2, X1, X0);
  nor nor_8 (ED0, NX2, NX1, X0);

  // Other names for the same wires on the sheet: NA0[6:0] = _7SA[6:0]; NA1[6:0] = _7SA[13:7]; NB0[6:0] = _7SB[6:0];
  //   NB1[6:0] = _7SB[13:7]; NC0[6:0] = _7SC[6:0]; NC1[6:0] = _7SC[13:7]; ND0[6:0] = _7SD[6:0]; ND1[6:0] = _7SD[13:7]
endmodule
