// Digital circuit Semaforo A.dig as structural Verilog
module Semaforo_A (
  input  Q0,
  input  Q1,
  input  Q2,
  input  Q3,
  input  NQ0,
  input  NQ1,
  input  NQ2,
  input  NQ3,
  output RA,
  output AA,
  output VA
);

  wire and_1_out;

  and and_1 (and_1_out, NQ1, NQ2, Q3);
  or or_1 (RA, Q1, Q2);
  or or_2 (AA, Q0, and_1_out);
  and and_2 (VA, NQ3, NQ2, NQ1, NQ0);
endmodule
