// Digital circuit Semaforo B.dig as structural Verilog
module Semaforo_B (
  input  Q0,
  input  Q1,
  input  Q2,
  input  Q3,
  input  NQ0,
  input  NQ1,
  input  NQ2,
  input  NQ3,
  output RB,
  output AB,
  output VB
);

  wire and_1_out, and_2_out, and_3_out, and_4_out, and_5_out;

  and and_1 (and_1_out, NQ3, Q2, Q1);
  and and_2 (and_2_out, NQ2, NQ3);
  and and_3 (and_3_out, NQ2, Q1);
  and and_4 (and_4_out, Q2, Q3);
  and and_5 (and_5_out, Q3, NQ0, NQ1);
  or or_1 (RB, and_1_out, Q0, and_2_out, and_3_out);
  or or_2 (AB, and_4_out, and_5_out);
  and and_6 (VB, Q2, NQ3, NQ1);
endmodule
