// Digital circuit Semaforo C.dig as structural Verilog
module Semaforo_C (
  input  Q0,
  input  Q1,
  input  Q2,
  input  Q3,
  input  NQ0,
  input  NQ1,
  input  NQ2,
  input  NQ3,
  output RC,
  output AC,
  output VC
);

  wire and_1_out, and_2_out, and_3_out, and_4_out, and_5_out, and_6_out, and_7_out;

  and and_1 (and_1_out, Q2, Q3, NQ1);
  and and_2 (and_2_out, Q3, NQ2, Q0);
  and and_3 (and_3_out, Q3, NQ2, Q1);
  and and_4 (and_4_out, NQ2, NQ1, NQ0);
  and and_5 (and_5_out, NQ3, Q2);
  and and_6 (and_6_out, Q1, Q2);
  and and_7 (and_7_out, NQ3, NQ1, Q0);
  and and_8 (VC, NQ2, NQ3, Q1);
  or or_1 (AC, and_1_out, and_2_out, and_3_out);
  or or_2 (RC, and_4_out, and_5_out, and_6_out, and_7_out);
endmodule
