// Digital circuit Semaforo D.dig as structural Verilog
module Semaforo_D (
  input  Q0,
  input  Q1,
  input  Q2,
  input  Q3,
  input  NQ0,
  input  NQ1,
  input  NQ2,
  input  NQ3,
  output RD,
  output AD,
  output VD
);

  wire and_1_out, and_2_out, and_3_out, and_4_out, and_5_out;

  and and_1 (and_1_out, NQ1, Q3);
  and and_2 (and_2_out, NQ3, NQ2, NQ0);
  and and_3 (and_3_out, NQ0, NQ1);
  and and_4 (and_4_out, Q0, NQ2, NQ3);
  and and_5 (and_5_out, Q3, Q1);
  or or_1 (RD, and_1_out, and_2_out, and_3_out);
  or or_2 (AD, and_4_out, and_5_out);
  and and_6 (VD, Q2, NQ3, Q1);
endmodule
