// Digital circuit Semaforo_Inteligente.dig as structural Verilog
module Semaforo_Inteligente (
  input  App,
  input  Ap,
  input  Al,
  input  All,
  input  clk_count,
  input  Bpp,
  input  Bp,
  input  Bl,
  input  Bll,
  input  Cpp,
  input  Cp,
  input  Cl,
  input  Cll,
  input  Dpp,
  input  Dp,
  input  Dl,
  input  Dll,
  input  clkMUX,
  output RB,
  output AB,
  output VB,
  output RA,
  output AA,
  output VA,
  output RD,
  output AD,
  output VD,
  output RC,
  output AC,
  output VC,
  output EA0,
  output EA1,
  output EB0,
  output EB1,
  output EC0,
  output EC1,
  output ED0,
  output ED1,
  output a,
  output b,
  output c,
  output d,
  output e,
  output f,
  output g
);

  wire _10_2_1__10_2, comparador_1_ta, comparador_1_tb, comparador_1_tc, comparador_1_td, NQ0, NQ1, NQ2, NQ3,
       Q0, Q1, Q2, Q3;
  wire [5:0] NA, NB, NC, ND;
  wire [13:0] _7SA, _7SB, _7SC, _7SD;

  Contador contador_1 (
    .clk_count(clk_count), .plus__plus(App), .plus(Ap), .in_4(Al), .in_6(All), .Num(NA), .NUM_7S(_7SA));
  Contador contador_2 (
    .clk_count(clk_count), .plus__plus(Bpp), .plus(Bp), .in_4(Bl), .in_6(Bll), .Num(NB), .NUM_7S(_7SB));
  Contador contador_3 (
    .clk_count(clk_count), .plus__plus(Cpp), .plus(Cp), .in_4(Cl), .in_6(Cll), .Num(NC), .NUM_7S(_7SC));
  Contador contador_4 (
    .clk_count(clk_count), .plus__plus(Dpp), .plus(Dp), .in_4(Dl), .in_6(Dll), .Num(ND), .NUM_7S(_7SD));
  Comparador comparador_1 (
    .NA(NA), .NB(NB), .NC(NC), .ND(ND), .TA(comparador_1_ta), .TB(comparador_1_tb), .TC(comparador_1_tc),
    .TD(comparador_1_td));
  MUX mux_1 (
    .clk_MUX(clkMUX), ._7SA(_7SA), ._7SB(_7SB), ._7SC(_7SC), ._7SD(_7SD), .a(a), .b(b), .c(c), .d(d), .e(e),
    .f(f), .g(g), .EA0(EA0), .EA1(EA1), .EB0(EB0), .EB1(EB1), .EC0(EC0), .EC1(EC1), .ED0(ED0), .ED1(ED1));
  _10_2 _10_2_1 (.clk_FSM(clk_count), ._10_2(_10_2_1__10_2));
  FSM fsm_1 (
    .clk_FF(_10_2_1__10_2), .TA(comparador_1_ta), .TB(comparador_1_tb), .TC(comparador_1_tc),
    .TD(comparador_1_td), .Q0(Q0), .Q1(Q1), .Q2(Q2), .Q3(Q3), .NQ0(NQ0), .NQ1(NQ1), .NQ2(NQ2), .NQ3(NQ3));
  Semaforo_A semaforo_a_1 (
    .Q0(Q0), .Q1(Q1), .Q2(Q2), .Q3(Q3), .NQ0(NQ0), .NQ1(NQ1), .NQ2(NQ2), .NQ3(NQ3), .RA(RA), .AA(AA), .VA(VA));
  Semaforo_B semaforo_b_1 (
    .Q0(Q0), .Q1(Q1), .Q2(Q2), .Q3(Q3), .NQ0(NQ0), .NQ1(NQ1), .NQ2(NQ2), .NQ3(NQ3), .RB(RB), .AB(AB), .VB(VB));
  Semaforo_C semaforo_c_1 (
    .Q0(Q0), .Q1(Q1), .Q2(Q2), .Q3(Q3), .NQ0(NQ0), .NQ1(NQ1), .NQ2(NQ2), .NQ3(NQ3), .RC(RC), .AC(AC), .VC(VC));
  Semaforo_D semaforo_d_1 (
    .Q0(Q0), .Q1(Q1), .Q2(Q2), .Q3(Q3), .NQ0(NQ0), .NQ1(NQ1), .NQ2(NQ2), .NQ3(NQ3), .RD(RD), .AD(AD), .VD(VD));
endmodule
