// Digital circuit bcd_7S.dig as structural Verilog
module bcd_7S (
  input  A,
  input  B,
  input  C,
  input  D,
  output [6:0] _7S
);

  wire and_1_out, and_2_out, and_3_out, and_4_out, and_5_out, and_6_out, and_7_out, and_8_out, and_9_out,
       and_10_out, and_11_out, and_12_out, and_13_out, and_14_out, and_15_out, and_16_out, and_17_out,
       and_18_out, and_19_out, and_20_out, and_21_out, and_22_out, and_23_out, and_24_out, and_25_out,
       and_26_out, and_27_out, and_28_out, and_29_out, and_30_out, NAP, NBP, NCP, NDP;

  not not_1 (NAP, A);
  not not_2 (NBP, B);
  not not_3 (NCP, C);
  not not_4 (NDP, D);
  and and_1 (and_1_out, B, NCP, D);
  and and_2 (and_2_out, A, NDP);
  and and_3 (and_3_out, B, C);
  and and_4 (and_4_out, A, NBP, NCP);
  and and_5 (and_5_out, NAP, C);
  and and_6 (and_6_out, NAP, B, D);
  and and_7 (and_7_out, NBP, NDP);
  and and_8 (and_8_out, NAP, C, D);
  and and_9 (and_9_out, NAP, NDP, NCP);
  and and_10 (and_10_out, NBP, NCP);
  and and_11 (and_11_out, NAP, NBP);
  and and_12 (and_12_out, NAP, NCP);
  and and_13 (and_13_out, NAP, D);
  and and_14 (and_14_out, NBP, NCP);
  and and_15 (and_15_out, NAP, B);
  and and_16 (and_16_out, NCP, NBP, NDP);
  and and_17 (and_17_out, A, NBP, D);
  and and_18 (and_18_out, NAP, NBP, C);
  and and_19 (and_19_out, B, C, NDP);
  and and_20 (and_20_out, A, NCP);
  and and_21 (and_21_out, NCP, NBP, NDP);
  and and_22 (and_22_out, NAP, C, NDP);
  and and_23 (and_23_out, NAP, NCP, NDP);
  and and_24 (and_24_out, NAP, B, NCP);
  and and_25 (and_25_out, NAP, B, NDP);
  and and_26 (and_26_out, A, NBP, NCP);
  and and_27 (and_27_out, NAP, NBP, C);
  and and_28 (and_28_out, NAP, NDP, C);
  and and_29 (and_29_out, NAP, B, NCP);
  and and_30 (and_30_out, A, NBP, NCP);
  or or_1 (_7S[1], and_8_out, and_9_out, and_10_out, and_11_out);
  or or_2 (_7S[2], and_12_out, and_13_out, and_14_out, and_15_out);
  or or_3 (_7S[3], and_16_out, and_17_out, and_1_out, and_18_out, and_19_out, and_20_out);
  or or_4 (_7S[4], and_21_out, and_22_out);
  or or_5 (_7S[5], and_23_out, and_24_out, and_25_out, and_26_out);
  or or_6 (_7S[6], and_27_out, and_28_out, and_29_out, and_30_out);
  or or_7 (_7S[0], and_2_out, and_3_out, and_4_out, and_5_out, and_6_out, and_7_out);

  // Other names for the same wires on the sheet: AP = A; BP = B; CP = C; DP = D
endmodule
