// Digital circuit div.dig as structural Verilog
module div (
  input  [5:0] NUM,
  output A0,
  output B0,
  output C0,
  output D0,
  output A1,
  output B1,
  output C1,
  output D1
);


  assign A0 = NUM[0];
  assign A1 = NUM[4];
  assign B0 = NUM[1];
  assign B1 = NUM[5];
  assign C0 = NUM[2];
  assign C1 = 1'b0;
  assign D0 = NUM[3];
  assign D1 = 1'b1;
endmodule
